# Fritzing sketch wiring (saved by Fritzing 0.9.3b)

parts:
  Part1 = Arduino Mega 2560 (Rev3)
  S1 = H-Bridge with L298N
  M2 = DC Motor
  TCRT1 = TCRT5000 digital module [part_number=151608]
  TCRT2 = TCRT5000 digital module [part_number=151608]
  TCRT3 = TCRT5000 digital module [part_number=151608]
  VCC1 = Battery block 9V
  M1 = DC Motor

nets:
  N1: Part1.A5, TCRT3.DO1
  N2: Part1.A6, TCRT2.DO1
  N3: Part1.A7, TCRT1.DO1
  5V: Part1.5V, S1.5V
  GND: Part1.GND, S1.GND, VCC1.-
  N4: Part1.D2_PWM, S1.ENA
  N5: Part1.D3_PWM, S1.IN1
  N6: Part1.D4_PWM, S1.IN2
  N7: Part1.D5_PWM, S1.IN3
  N8: Part1.D6_PWM, S1.IN4
  N9: Part1.D7_PWM, S1.ENB
  N10: S1.12V, VCC1.+
  N11: S1.M1-01, M2.pin_2
  N12: S1.M1-02, M2.pin_1
  N13: S1.M2-01, M1.pin_2
  N14: S1.M2-02, M1.pin_1

custom parts:
  H-Bridge with L298N: h-bridge
  TCRT5000 digital module: breakout board for TCRT5000 module, convert analog to digital - Uses TCRT5000 infrared reflectance sensor - Detection distance: 1mm~8mm - Focus distance: 2.5mm - Working voltage: 3.3V~12V - Uses wide voltage LM393 comparator - With multi-turn precision potentiometer to adjust the sensitivity - Current: > 15mA - Output type: Digital switch output (0, 1) - Suitable for watt-hour meter pulse data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
